// Digital circuit MUX.dig as structural Verilog
module MUX (
  input  D,
  input  C,
  input  B,
  input  A,
  output Y
);

  wire not_1_out, not_2_out;

  not not_1 (not_1_out, D);
  not not_2 (not_2_out, D);
  Multiplexer #(.Selector_Bits(3)) multiplexer_1 (
    .sel({A, B, C}), .in_0(1'b1), .in_1(D), .in_2(D), .in_3(D), .in_4(not_1_out), .in_5(not_2_out),
    .in_6(1'b1), .in_7(1'b0), .out(Y));

  // Notes on the sheet:
  //   Use A as the most-significant bit and 
  //   D as the least-significant bit.
  //   Converts between single bits & a 3-bit bus
endmodule

/* Test case:
A B C D Y
0 0 0 0 X
0 0 0 1 1
0 0 1 0 0 
0 0 1 1 1 
0 1 0 0 0 
0 1 0 1 1 
0 1 1 0 0 
0 1 1 1 1 
1 0 0 0 1 
1 0 0 1 0 
1 0 1 0 1 
1 0 1 1 0
1 1 0 0 1 
1 1 0 1 X 
1 1 1 0 X 
1 1 1 1 X
*/
